# Fritzing sketch Schematic (saved by Fritzing 0.9.3b)
breadboards: 1

parts:
  Slave = Arduino Uno (Rev3) - ICSP
  Master = Arduino Uno (Rev3) - ICSP
  part = RFID-RC522
  J1 = Piezo Speaker
  Switch_One = Pushbutton [package="[THT]"]
  Switch_Two = Pushbutton [package="[THT]"]
  part_2 = Basic Servo
  part_3 = Basic Servo
  part_4 = Resistor [tolerance=±5% resistance=10k package="0603 [SMD]"]
  part_5 = Resistor [tolerance=±5% resistance=10k package="0603 [SMD]"]
  Switch_Resistors = KENT_LCD_CONN [package=ffc_16]
  part_6 = Bluetooth HC-05 Macho
  part_7 = Bluetooth HC-05 Macho

nets:
  N1: Slave.A0, part_3.pulse
  VCC: Slave.5V, part_3.vcc, part_7.VCC
  GND: Slave.GND, part_3.gnd, part_7.GROUND
  N2: Slave.D2, part_7.TXD
  N3: Slave.D3_PWM, part_7.RXD
  N4: Master.A0, J1.pin1
  GND_2: Master.GND, J1.pin2, Switch_One.Pin_1, Switch_One.Pin_2, part_2.gnd, Switch_Resistors.GND, part_6.GROUND
  VCC_2: Master.5V, part_2.vcc, part_4.Pin_0, part_5.Pin_0, Switch_Resistors.+5V, Switch_Resistors.BL, part_6.VCC
  N5: Master.ICSP2_SCK, Switch_Resistors.SCK
  N6: Master.ICSP2_MOSI, Switch_Resistors.MOSI
  N7: Master.D8, Switch_Resistors.CS-LD
  N8: Master.D9_PWM, part.SDA
  N9: Master.D10_PWM/SS, part.GND
  N10: Master.D11_PWM/MOSI, part.MOSI
  N11: Master.D12/MISO, part.MISO
  N12: Master.D13/SCK, part.SCK
  N13: Master.A5/SCL, part_2.pulse
  N14: Master.D2, Switch_One.Pin_3, Switch_One.Pin_4, part_5.Pin_1
  N15: Master.D3_PWM, Switch_Two.Pin_3, Switch_Two.Pin_4, part_4.Pin_1
  N16: Master.D4, part_6.TXD
  N17: Master.D5_PWM, part_6.RXD
  N18: Master.D6_PWM, Switch_Resistors.RESET
  N19: Master.D7, Switch_Resistors.D/C-LD
  3V3: Master.3V3, part.3.3V

custom parts:
  KENT_LCD_CONN: Connector for Kent display (LCD-09560)
